# Fritzing sketch Componentes_Varios (saved by Fritzing 0.9.6b)

parts:
  LM1 = RioRand LM2596  # not connected
  Battery_2200mAh1 = LIPO-2200mAh [package=lipo-2200]  # not connected
  JUMPER1 = JUMPER [package=JUMPER]  # not connected
  L298N-PONTEH1 = PONTE H - L298N  # not connected
  Motor_DC_Esquerdo1 = Motor DC 6V Esquerdo  # not connected
  Power_plug1 = Power plug  # not connected
  MOTOR_DC_6V_direito1 = MOTOR_DC6V  # not connected
  KY-3 = Keyes Relay [package=THT]  # not connected
  U2 = NodeMCU V1.0  # not connected
  LED3 = LEDs [package=led10mm]  # not connected
  Part3 = Lilypad Battery Connect  # not connected
  Part4 = KY-019 5V Relay Module [package="Breakout board"]  # not connected
  Part5 = KY-012 Active Buzzer Module [package="Breakout board"]  # not connected
  Part6 = Arduino Nano (Rev3.0)  # not connected
  Generic_4x4_button_keypad1 = Generic 4x4 Keypad  # not connected
  USBTTL1 = USB TTL Serial Cable  # not connected
  Matrix_keypad3 = KEYPAD 4x4  # not connected
  Keypad4x1 = Keypad Membran 4x4  # not connected
  SPKR1 = Loudspeaker  # not connected
  J1 = Piezo Speaker  # not connected
  SP1 = SPEAKER [package=pcb_mount_speaker]  # not connected
  Componente19 = Jtron 1 Channel Optoisolated Relay Module [package=relay]  # not connected
  LCD2 = LCD screen  # not connected
  LCM1602_IIC1 = LCM1602 IIC [part_number="LCM1602 IIC" chip_label="LCM1602 IIC" package="DIP (Dual Inline) [THT]"]  # not connected
  U5 = LCD-16X2 [package=lcd-16x2_noholes]  # not connected
  LCD2004-I2C1 = LCD2004-I2C  # not connected
  Componente20 = LCD1602-I2C  # not connected
  YwRobot_Power_Supply1 = YwRobot Breadboard Power Supply [part_number=545043]  # not connected
  M3 = fc-51 [package=THT]  # not connected
  R1 = TI196-p  # not connected
  BT1 = Bluetooth HC-06u [package=THT]  # not connected
  Componente21 = Bluetooth HC-05 Macho  # not connected
  Componente22 = Bluetooth HC-06  # not connected
  Teensy1 = Teensy 3.6 (Basic)  # not connected
  Componente23 = SD Micro-SD Card  # not connected
  Componente24 = LCD Keypad Shield  # not connected
  Sensor1 = TTP223B Capacitive Touch Sensor Module  # not connected
  J10 = AVR ISP 6 Pin [package=2x3_offset]  # not connected
  F1 = Fan - Ventilador [package=THT]  # not connected
  J11 = Fluke 17B+ DIGITAL MULTIMETER [form="♀ (female)" package=THT]  # not connected
  FTDI_USB_UART1 = CP2102 USB UART [part_number="USB UART"]  # not connected
  C1 = Cappy the Capacitor  # not connected
  LED4 = Billie the Blue LED  # not connected
  LED5 = Gus the Green LED  # not connected
  LED6 = Ruby the Red LED  # not connected
  U6 = tda7294V [package=THT]  # not connected
  Sw1 = SS13D01  # not connected
  Componente25 = songle relay  # not connected
  SIM800L_BO1 = SIM800L BO  # not connected
  J12 = 3.5mm Switch Jack  # not connected
  J13 = Raspberry Pi Header 40pin [package=THT]  # not connected
  Mod1 = RPI Grove Base HAT  # not connected
  Mod2 = Raspberry Pi 4B  # not connected
  S1 = Pushbutton horitzontal [package="[THT]"]  # not connected
  S2 = Pushbutton horitzontal [package=THT]  # not connected
  LDR1 = Photocell (LDR) [package=THT]  # not connected
  OLED1 = OLED 128x64 I2C Monochrome Display VDD-GND  # not connected
  Squix1 = OLED 0.96" 128x64 I2C SSD1306  # not connected
  OLED2 = OLED 128x64 I2C Monochrome Display GND-VDD  # not connected
  Ohmmeter1 = Ohmmeter  # not connected
  VM1 = Multimeter (DC Voltage)  # not connected
  Componente26 = Mikrobus Prototype Board  # not connected
  Componente27 = Matrix LED de 8x8 basada en MAX7219  # not connected
  Part7 = KY-015 Temperature & Humidity Sensor Module [package="Breakout board"]  # not connected
  IR_Receiver1 = IR_Receiver  # not connected
  U7 = ina125P [package="DIP16 [THT]"]  # not connected
  M4 = Humidity and Temperature Sensor DHT11  # not connected
  M5 = Getriebemotor  # not connected
  J14 = male pin header, 8 pins [form="♂ (male)"]  # not connected
  Componente28 = Switch Science FDTI USB-Serial adapter  # not connected
  U8 = ESP8266-01S [part_number=ESP8266]  # not connected
  U9 = ESP8266 WiFi Module [part_number=ESP8266]  # not connected
  U10 = ESP8266 ESP-01 Upgraded WiFi Module [part_number=ESP8266]  # not connected
  M6 = DOIT Esp32 DevKit v1 (30 pins long, 11 pins width) [part_number=ESP32S-PIN30]  # not connected
  IC1 = DIP-16-oblong-pads [package="DIP (Dual Inline) [THT]"]  # not connected
  J15 = DHT22 temperature-humidity sensor [form="♂ (male)" package=THT]  # not connected
  J16 = DHT11 basic temperature-humidity sensor [form="♂ (male)" package=THT]  # not connected
  M7 = DC Mini Metal Gear Motor  # not connected
  M8 = Portenta-h7  # not connected
  RLY1 = Relay [part_number=JQC-3F package=THT]  # not connected
  R2 = Trimmer Potentiometer [package=THT]  # not connected
  ZIF_SOCKET1 = Aries 28-6574-10 28W ZIF Socket [part_number=28-6574-10]  # not connected
  IC2 = ZS-042 RTC Module  # not connected
  DHT2 = DHT22 Humidity and Temperature Sensor  # not connected
  ZIF1 = ZIF_Blue [part_number=TFXTOOL-228-3341]  # not connected
  Mod3 = Raspberry Pi Pico  # not connected
  Espessif_Serial_Wifi_Modul_1 = ESP8266 ESP01 [part_number=ESP8266 package=THT]  # not connected
  Mod4 = Full Size SD Card Module  # not connected
  Mod5 = L298N DC motor driver  # not connected
  Driver1 = 28BYJ-48 Driver Module [part_number=ULN2003 package=THT]  # not connected
  SM1 = 28BYJ-48 Stepper Motor [part_number=28BYJ-48]  # not connected
  M9 = Hobby Gearmotor with 48:1 gearbox [part_number=ROB-13302]  # not connected
  MOTOR1 = Adafruit Gear-Reduced Stepper Motor (small)  # not connected
  Power_plug2 = USB-C plug  # not connected
  LCD3 = 1_7in tft lcd  # not connected
  IC3 = NXP MK20DX256VLH7 [package=LQFP64]  # not connected
  M10 = ESP-Prog [package=THT]  # not connected
  Mod6 = Nano-V3-0-IO-Expansion-Adapter
  Componente29 = Arduino Nano (Rev3.0)
  U11 = ESP32-38PinWide [part_number=ESP32-38PinWide]  # not connected
  SparkFun_ESP32_Thing_Plus1 = SparkFun ESP32 Thing Plus [part_number=14689]  # not connected
  ESP32_LoRa_1_Channel_Gateway1 = SparkFun ESP32 LoRa_1 Channel Gateway [part_number=15006]  # not connected
  Componente30 = Adafruit HUZZAH32 ESP32 Feather [part_number="Adafruit #3405"]  # not connected
  M11 = Arduino NANO RP2040 CONNECT with headers  # not connected
  M12 = Arduino Nano 33 IOT-tht  # not connected
  Mod7 = seeeduino-xiao  # not connected
  M13 = cc1101 module  # not connected
  GSM_SIM_GPSR_SMS_SIM900_SIM1 = SIM800L [package=THT]  # not connected
  Componente31 = node32s  # not connected
  MCU1 = ESP-WROVER-B Module [part_number=ESP-WROVER-B]  # not connected
  M14 = FireBeetle ESP32-E  # not connected
  Componente32 = nRF52 DK  # not connected
  M15 = SHT35-D [package="SIP (Single Inline) [THT]"]  # not connected
  U12 = mcu8266 [package=dil40_0.9]  # not connected
  Squix2 = nokia lcd 5110  # not connected
  M16 = ac light dimmer-4terminal  # not connected
  R3 = b503 pot  # not connected
  SW2 = DIP SWITCH [package=dipswitch-02]  # not connected
  SW3 = DIP Switch 4 Position [package=dipswitch-04]  # not connected
  Intesc1 = Mod DIP [package="DIP (Dual Inline) [THT]"]  # not connected
  S3 = DIP Switch 3 Position  # not connected
  SW1 = DIP Switch 8 Position [package=dipswitch-08]  # not connected

nets:
  VCC: Mod6.VCC, Componente29.5V
  GND: Mod6.GND, Componente29.GND
  N1: Mod6.D13/SCK, Componente29.D13/SCK
  N2: Mod6.NC, Componente29.3V3
  N3: Mod6.AREF, Componente29.AREF
  N4: Mod6.A0, Componente29.A0
  N5: Mod6.A1, Componente29.A1
  N6: Mod6.A2, Componente29.A2
  N7: Mod6.A3, Componente29.A3
  N8: Mod6.A4/SDA, Componente29.A4
  N9: Mod6.A5/SCL, Componente29.A5
  N10: Mod6.A6, Componente29.A6
  N11: Mod6.A7, Componente29.A7
  N12: Mod6.RST, Componente29.RESET
  VIN: Mod6.VIN, Componente29.VIN
  N13: Mod6.D12/MISO, Componente29.D12/MISO
  N14: Mod6.D11_PWM/MOSI, Componente29.D11/MOSI
  N15: Mod6.D10_PWM/SS, Componente29.D10
  N16: Mod6.D9_PWM, Componente29.D9
  N17: Mod6.D8, Componente29.D8
  N18: Mod6.D7, Componente29.D7
  N19: Mod6.D6_PWM, Componente29.D6
  N20: Mod6.D5_PWM, Componente29.D5
  N21: Mod6.D4, Componente29.D4
  N22: Mod6.D3_PWM, Componente29.D3
  N23: Mod6.D2, Componente29.D2
  N24: Mod6.D0/RX, Componente29.D0/RX
  N25: Mod6.D1/TX, Componente29.D1/TX

notes:
  Bateria 11,3V
  Puente H L298N
  Regulador de Voltaje LM2596s
  Jumper - Puente H
  Plug
  Motor DC 6V Derecho
  Motor DC 6V Izquierdo

custom parts:
  LIPO-2200mAh: 2200mAh Lipo-battery
  PONTE H - L298N: PONTE H
  Motor DC 6V Esquerdo: Motor dc esquerdo
  Power plug: power plug
  MOTOR_DC6V: Motor dc 6V direito
  Keyes Relay: The Keyes 5V relay module is suitable for SCM development, home appliance control. It uses a 5V~12V TIL control signal which can control DC / AC signal.
  NodeMCU V1.0: ESP9266 based NodeMCU
  KY-019 5V Relay Module: KY-019 5V Relay module, used to control AC circuits.
  KY-012 Active Buzzer Module: Active Piezoelectric Buzzer Module Keyes KY-012, it produces single-tone sound when signal is high.
  Generic 4x4 Keypad: generic 4x4 keypad 4 rows of four 6 mm tact switches cheap and nasty but works
  KEYPAD 4x4: Matrix keypad 16 buttons, 4 rows x 4 columns
  Keypad Membran 4x4: Membrane Keypad 4x4 Matrix
  LCM1602 IIC: I2C-Module to use a 1602 or 2004 LCD on with the wire.h libory Serial LCD Modul
  LCD2004-I2C: A standard character display with 4x20 characters. Comes in many colors with LCM2004 IIC attached.
  LCD1602-I2C: A standard character display, usually with 2x16 characters. Comes in many colors with LCM1602 IIC attached.
  YwRobot Breadboard Power Supply: The YwRobot Breadboard Power Supply (MB-V2) has two power rails; they can be 5V or 3V3. Power to the module can be provided through the female USB socket or through the A10 (female) 2.1mm power jack.
  TI196-p: SRPassives t196-p trimpot
  Bluetooth HC-06u: Bluetooth HC-06 - face up, pins down 16.5mm x 37.5mm PCB
  Teensy 3.6 (Basic): The Teensy is a complete USB-based microcontoller development system, in a very small footprint, capable of implementing many types of projects. All programming is done via the USB port. No special programmer is needed, only a standard micro-USB cable and a PC or Macintosh with a USB port.
  SD Micro-SD Card: Breakout board Platform Based On Arduino by Iteadstudio Principal features : Electronic Brick Ports 3.3V or 5V power supply The official support forum: support@iteadstudio.com
  LCD Keypad Shield: It consists of a 1602 white character blue backlight LCD. The keypad consists of 5 keys — select, up, right, down and left. To save the digital IO pins, the keypad interface uses only one ADC channel. The key value is read through a 5 stage voltage divider.
  TTP223B Capacitive Touch Sensor Module: The TTP223B capacitive touch sensor module uses the TTP223B IC. The appropriate voltage is approximately 2 to 5.5 volts.
  Fan - Ventilador: Ventilador de 2 pines, se encuentra comunmente en computadoras de escritorio
  Fluke 17B+ DIGITAL MULTIMETER: Generic female header
  CP2102 USB UART: CP2102 USB UART FTDI
  Cappy the Capacitor: Cappy E. Lectrifield, a polarized electrolytic capacitor
  tda7294V: 100V 100W DMOS Audio Power amplifier with mute/st-by.
  SS13D01: Side-actuated SPDT slide switch, as used on the Arduino Pro
  3.5mm Switch Jack: Distrelec Schweiz 3.5mm mono switching Jack
  Raspberry Pi Header 40pin: Raspberry Pi 40 pin header - for creating your own shields. (Mar 2020, bb: make breadboard friendly (.4in pin spacing) and add labels. Schematic add labels. PCB make oblong pins to allow routing traces between the pins.)
  RPI Grove Base HAT: Seeed Raspberry Pi Grove Base HAT v1.0.
  Pushbutton horitzontal: A generic horizontal pushbutton.
  Pushbutton horitzontal: A generic pushbutton with horizontal button orientation.
  Photocell (LDR): A generic light dependent resistor (LDR)
  OLED 128x64 I2C Monochrome Display VDD-GND: OLED 128x64 I2C Monochrome Display. Note: there are two variants of this part, this one is the VDD GND SCK SDA variant. The other is GND VDD SCK SDA. Make sure you select the part that matches your module as using the incorrect part will probably destroy your module! In addition the mounting holes are marked on silkscreen but not by default drilled. If you want drilled mounting holes, copy a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
  OLED 128x64 I2C Monochrome Display GND-VDD: OLED 128x64 I2C Monochrome Display. Note: there are two variants of this part, this one is the GND VDD SCK SDA variant. The other is VDD GND SCK SDA. Make sure you select the part that matches your module as using the incorrect part will probably destroy your module! In addition the mounting holes are marked on silkscreen but not by default drilled. If you want drilled mounting holes, copy a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
  Ohmmeter: A Standard Multimeter in Current mode
  Mikrobus Prototype Board: Mikrobus Prototype board
  KY-015 Temperature & Humidity Sensor Module: KY-015 temperature and humidity sensor module, provides a low-latency serial interface to measure humidity and temperature.
  IR_Receiver: 赤外線受信モジュール GP1UXC41QS
  ina125P: High accuracy instrumentation amplifier.
  Humidity and Temperature Sensor DHT11: Digital relative humidity & temperature sensor DHT11
  Switch Science FDTI USB-Serial adapter: https://www.switch-science.com/catalog/1032/
  ESP8266 WiFi Module: Generic WiFi Module based on the ESP8266 with onboard PCB antenna and UART communications
  ESP8266 ESP-01 Upgraded WiFi Module: Upgraded Version ESP-01,all Flash are upgraded to 1M byte.Also support Cloud service remote transmission.
  DOIT Esp32 DevKit v1 (30 pins long, 11 pins width): The DOIT Esp32 DevKit v1 is one of the development board created by DOIT to evaluate the ESP-WROOM-32 module. It is based on the ESP32 microcontroller that boasts Wifi, Bluetooth, Ethernet and Low Power support all in a single chip. (vanepp) made breadboard work, adjusted pin numbering and labels and reduced size of schematic and cleaned up pcb. This chip is 30pins long (2 x15) and 11 pins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
  DIP-16-oblong-pads: A DIP stand-in part for whatever IC you want. With 16 pins on a 300mil dual inline package (DIP) footprint with oblong pads.
  DHT22 temperature-humidity sensor: The DHT22 is a basic, low-cost digital temperature and humidity sensor. It uses a capacitive humidity sensor and a thermistor to measure the surrounding air, and spits out a digital signal on the data pin (no analog input pins needed). It's fairly simple to use, but requires careful timing to grab data. The only real downside of this sensor is you can only get new data from it once every 2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
  DHT11 basic temperature-humidity sensor: The DHT11 is a basic, ultra low-cost digital temperature and humidity sensor. It uses a capacitive humidity sensor and a thermistor to measure the surrounding air, and spits out a digital signal on the data pin (no analog input pins needed). Its fairly simple to use, but requires careful timing to grab data. The only real downside of this sensor is you can only get new data from it once every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
  Portenta-h7: arduino Portenta H7 ST STM32H747XI processor Dual core Cortex M7 2M flash 1M ram. Note this part does not include the 2 high density connectors, only the 28 breadboard connectors!
  Relay: An SPDT relay.
  Trimmer Potentiometer: A standard 6mm trimmer potentiometer.
  ZIF_Blue: ZIF connector, 28 pin
  Raspberry Pi Pico: Raspberry Pi Pico. Based around the RP2040 microcontroller the Pico is a low cost microcontroller device bringing Raspberry Pi quality, cost, and easy of use to the microcontroller space. Jan 2021, Split part in to two versions: tht (this one) and SMD. This one will drill holes for a .1 in header in pcb to allow plugging in the module as well as providing pads to solder the module to the top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
  ESP8266 ESP01: Generic WiFi Module based on the ESP8266 with onboard PCB antenna and UART communications
  Full Size SD Card Module: SD Card Module Slot Socket Reader For Arduino ARM MCU
  L298N DC motor driver: 2x DC motor driver with 78M05 positive voltage regulator (7..35 V) L298N: max 46 V, 2 A Set 5 V Enable jumper to enable 5 V regultor (needed for the L298N) and +5 V output at screw terminal or supply external +5 V at screw terminal Set ENA and/or ENB to +5 V to enable motor permanently or supply ENA and/or ENB with PWM signal IN1 and IN2 set rotation directory for motor A (OUT1/OUT2) IN2 and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
  28BYJ-48 Driver Module: Generic male header
  28BYJ-48 Stepper Motor: Unipolar Stepper Motor 28BYJ-48 Top coil - pink & orange Bottom coil - blue & yellow Common rail - red Connector pins: blue - pink - yellow - orange - red
  Adafruit Gear-Reduced Stepper Motor (small): Adafruit gear-reduction stepper motor (small)
  USB-C plug: power plug
  1_7in tft lcd: This is the Zoll 1.77in spi lcd display. The 1.77" display has 128x160 color pixels.
  NXP MK20DX256VLH7: ARM Microcontrollers KINETIS 256K, manufactured by NXP / Freescale
  ESP-Prog: Espressif ESP-Prog board. ESP-Prog is one of Espressif’s development and debugging tools, with functions including automatic firmware downloading, serial communication, and JTAG online debugging. ESP-Prog's automatic firmware downloading and serial communication functions are supported on both the ESP8266 and ESP32 platforms, while the JTAG online debugging is supported only on the ESP32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
  Nano-V3-0-IO-Expansion-Adapter: Nano V3.0 IO Expansion Adapter Shield. Note pcb view has been supressed as not useful. You can drag a Nano over the Nano connectors and it will connect and appear in schematic (although at present due to a bug, routing will not show as complete in breadboard).
  ESP32-38PinWide: Generic 38-Pin ESP32 with wide format (only access to one side of pins on a breadboard) based on Stephen Lilley's HiLetgo ESP-WROOM-32 ESP32 ESP-32S Development Board.
  SparkFun ESP32 Thing Plus: The SparkFun ESP32 Thing Plus enjoys all the amenities of the ESP32 Thing, but with a few added sparkles. We've lengthened the board just a bit to accommodate a Qwiic connector for all your Qwiic breakout needs. We've also moved a few pins around to make the board compatible with the Adafruit Huzzah32 – ESP32 Feather Board such that you can use all of those lovely shields available out there!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
  SparkFun ESP32 LoRa_1 Channel Gateway: The SparkFun 1-Channel LoRa Gateway is a powerful 3-network capable device thanks to an onboard ESP32 WROOM module and an RFM95W LoRa modem. The RFM95W handles the 915MHz band while the ESP32 takes care of Bluetooth and WiFi capabilities. One of the ideal uses is to convert LoRa (Long Range) radio messages into data packets that you can access via the web, but of course the flexibility it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
  Arduino NANO RP2040 CONNECT with headers: Meet the only connected RP2040 board. It fits the Arduino Nano form factor, making it a small board with BIG features. The brain of the board is the Raspberry Pi RP2040 silicon; a dual-core Arm Cortex M0+ running at 133MHz. It has 264KB of SRAM, and the 16MB of flash memory is off-chip to give you extra storage. But what’s really exciting is the on-board connectivity options. The hugely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
  Arduino Nano 33 IOT-tht: The Arduino Nano 33 IoT is the easiest and cheapest point of entry to enhance existing devices (and creating new ones) to be part of the IoT and designing pico-network applications. Whether you are looking at building a sensor network connected to your office or home router, or if you want to create a BLE device sending data to a cellphone, the Nano 33 IoT is your one-stop-solution for many of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
  seeeduino-xiao: Seeeduino XIAO processor board.
  cc1101 module: CC1101 rf module.
  ESP-WROVER-B Module: Espressif ESP-WROVER-B WiFi-BT-BLE microcontroller module. The ESP32 is a microcontroller chip with WiFi and BLE capabilities. The chip is developed by Espressif and is the successor to the popular ESP8266 WiFi module.
  FireBeetle ESP32-E: FireBeetle ESP32-E, specially designed for IoT, is an ESP-WROOM-32E-based main controller board with dual-core chips. It supports WiFi and Bluetooth dual-mode communication and features a small size, ultra-low power consumption, on-board charging circuit, and easy-to-use interface, which can be conveniently used for smart home IoT, industrial IoT applications, wearable devices, and so on. You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
  nRF52 DK: The nRF52 DK is a versatile single board development kit for Bluetooth® Smart, ANT and 2.4GHz proprietary applications using the nRF52832 SoC. This kit supports development for the nRF52832 SoC. The kit is hardware compatible with the Arduino Uno Revision 3 standard, making it possible to use 3rd-party shields that are compatible to this standard. An NFC antenna can be connected the kit to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
  SHT35-D: SHT35-D is an I2C connected temperature and humidity sensor
  nokia lcd 5110: nokia 5110
  ac light dimmer-4terminal: ac light dimmer module 4terminal.
  b503 pot: B503 Pot.
  Mod DIP: Módulo de Dip Swtich - 8
