# Fritzing sketch MP1584EN (saved by Fritzing 0.9.4)
circuit board: 17.03cm x 10.2401cm

parts:
  A_Nano = Arduino Nano (Rev3.0)
  SDA_D3 = RJ45 Jack [package=rj45-8]
  SDA_D5 = RJ45 Jack [package=rj45-8]
  SDA_D2 = RJ45 Jack [package=rj45-8]
  SDA_D4 = RJ45 Jack [package=rj45-8]
  MP1584EN_9V-5V = MP1584EN Power Regulator Board [part_number=MP1584EN]
  LD1117VXX = V_REG_LD1117VXX [package=78xxl]
  KY040 = Generic female header - 5 pins [form="♀ (female)" package=THT]

nets:
  GND: A_Nano.GND, SDA_D3.6, SDA_D5.6, SDA_D2.6, SDA_D4.6, MP1584EN_9V-5V.OUT_-, LD1117VXX.GND, KY040.GND
  N1: A_Nano.D2, SDA_D2.1
  N2: A_Nano.D3, SDA_D3.1
  N3: A_Nano.D4, SDA_D4.1
  N4: A_Nano.D5, SDA_D5.1
  N5: A_Nano.D6, KY040.CLK
  N6: A_Nano.D7, KY040.DT
  D8 Bus: A_Nano.D8, SDA_D3.7, SDA_D5.7, SDA_D2.7, SDA_D4.7
  MOSI: A_Nano.D11/MOSI, SDA_D3.3, SDA_D5.3, SDA_D2.3, SDA_D4.3
  MISO: A_Nano.D12/MISO, SDA_D3.4, SDA_D5.4, SDA_D2.4, SDA_D4.4
  N7: A_Nano.VIN, MP1584EN_9V-5V.OUT_+#16
  5V: A_Nano.5V, KY040.+
  SCK: A_Nano.D13/SCK, SDA_D3.2, SDA_D5.2, SDA_D2.2, SDA_D4.2
  3.3V: SDA_D3.8, SDA_D5.8, SDA_D2.8, SDA_D4.8, LD1117VXX.OUT
  N8: MP1584EN_9V-5V.OUT_+#15, LD1117VXX.IN

notes:
  9v PSU
  5v GND/VCC directly to arduino
  5v GND/VCC to regulator 3,3v OUT

custom parts:
  MP1584EN Power Regulator Board: The MP1584EN is a high frequency step-down switching regulator. The input voltage range is 4.5V to 28V. The output voltage is set by the board's potentiometer.
  Generic female header - 5 pins: Generic female header
