# Fritzing sketch Puntas Multimetro (saved by Fritzing 0.9.4)
breadboards: 1

parts:
  VM1 = Multimeter (DC Voltage)
  P1 = Multimeter straight red probe
  P2 = Multimeter straight black probe
  IC1 = IC, DIP package, 8 pins [chip_label=IC]
  VM2 = Multimeter (DC Voltage)
  IC2 = IC, DIP package, 8 pins [chip_label=IC]
  P3 = Multimeter straight red probe
  P4 = Multimeter straight black probe

nets:
  N1: VM1.COM_Probe, P2.Probe_tip, P2.Probe_meter_end, IC1.pin4
  N2: VM1.V_Probe, P1.Probe_tip, P1.Probe_meter_end, IC1.pin8
  N3: VM2.COM_Probe, IC2.pin4, P4.Probe_tip, P4.Probe_meter_end
  N4: VM2.V_Probe, P3.Probe_meter_end

custom parts:
  Multimeter straight red probe: A standard multimeter straight red probe.
  Multimeter straight black probe: A standard multimeter straight black probe.
